// Logisim project 3.1_half_adder_NAND.circ as structural Verilog: 3 circuits, main circuit main
module main (
  input  A,
  input  B,
  output S,
  output C,
  output S_2,
  output C_2
);

  original original_1 (.A(A), .B(B), .S(S), .C(C));
  NAND_implementation nand_implementation_1 (.A(A), .B(B), .S(S_2), .C(C_2));
endmodule

module original (
  input  A,
  input  B,
  output S,
  output C
);

  xor xor_1 (S, A, B);
  and and_1 (C, A, B);
endmodule

module NAND_implementation (
  input  A,
  input  B,
  output S,
  output C
);

  wire A__BB_out, A_A_out, A_B_out, B__AA_out, B_B_out;

  nand A_B (A_B_out, B, A);
  nand A_A (A_A_out, A, A);
  nand B_B (B_B_out, B, B);
  not AB___AB (C, A_B_out);  // NAND_Gate
  nand A__BB (A__BB_out, A, B_B_out);
  nand B__AA (B__AA_out, A_A_out, B);
  nand nand_1 (S, A__BB_out, B__AA_out);
endmodule
