// Logisim project D-Latch.circ as structural Verilog: 1 circuit, main circuit main
module main (
  input  en,
  input  D,
  output Q,
  output Q_minus
);

  wire nand_1_out, nand_2_out, not_1_out;

  not not_1 (not_1_out, D);
  nand nand_1 (nand_1_out, en, D);
  nand nand_2 (nand_2_out, not_1_out, en);
  nand nand_3 (Q, nand_1_out, Q_minus);
  nand nand_4 (Q_minus, Q, nand_2_out);
endmodule
